# Fritzing sketch schematics (saved by Fritzing 0.9.6b)
breadboards: 1

parts:
  R1 = Resistor [tolerance=±5% resistance=100k package=THT]
  R2 = Resistor [tolerance=±5% resistance=100k package=THT]
  R3 = Resistor [tolerance=±5% resistance=100k package=THT]
  Q_MAIN = MOSFET-NCHANNEL [package=to220v]
  V1 = DC Power [voltage=5V]
  LCD1 = LCD1602-I2C
  U1 = NodeMCU V1.0
  R4 = Resistor [tolerance=±5% resistance=100k package=THT]
  Q_HOLD = Basic FET P-Channel [package="TO220 [THT]"]
  R5 = Resistor [tolerance=±5% resistance=100k package=THT]
  Q_ON = Basic FET N-Channel [package="D2Pak [SMD]"]
  R6 = Resistor [tolerance=±5% resistance=100k package=THT]
  R7 = Resistor [tolerance=±5% resistance=100k package=THT]
  R8 = Resistor [tolerance=±5% resistance=7k package=THT]

nets:
  GND: R1.Pin_0, R2.Pin_0, R3.Pin_0, Q_MAIN.D, LCD1.GND, U1.GND
  Row 2: R1.Pin_1, U1.D8
  Row 3: R2.Pin_1, U1.D6
  Row 4: R3.Pin_1, U1.D5
  N1: Q_MAIN.G, R4.Pin_1, Q_HOLD.drain
  N2: Q_MAIN.S, V1.V-, R4.Pin_0, Q_ON.source, R6.Pin_0
  Col 4: V1.V+, LCD1.VCC, U1.Vin, Q_HOLD.source, R5.Pin_0
  N3: LCD1.SDA, U1.D2
  N4: LCD1.SCL, U1.D1
  Col 1: U1.D0
  Col 3: U1.D3
  Col 2: U1.D4
  N5: U1.D7, R8.Pin_0
  N6: U1.RX, Q_HOLD.gate, R5.Pin_1, Q_ON.drain
  N7: Q_ON.Gate, R6.Pin_1, R7.Pin_0
  Row 1: R7.Pin_1, R8.Pin_1

custom parts:
  LCD1602-I2C: A standard character display, usually with 2x16 characters. Comes in many colors with LCM1602 IIC attached.
  NodeMCU V1.0: ESP8266 based NodeMCU
